// Logisim project SYC.circ as structural Verilog
module Bramka_OR (
  input  in_1,
  input  in_2,
  output out_3
);

  wire not_1_out, not_2_out;

  not not_1 (not_1_out, in_1);
  not not_2 (not_2_out, in_2);
  nand nand_1 (out_3, not_1_out, not_2_out);
endmodule

module Bramka_AND (
  input  in_1,
  input  in_2,
  output out_3
);

  wire nand_1_out;

  nand nand_1 (nand_1_out, in_1, in_2);
  not not_1 (out_3, nand_1_out);
endmodule

module Bramka_NOT (
  input  in_1,
  output out_2
);

  nand nand_1 (out_2, in_1, in_1);
endmodule

module przyklad (
  input  a,
  input  b,
  input  c,
  output y
);

  wire and_1_out, nand_1_out, xor_1_out;

  and and_1 (and_1_out, c, ~b);  // AND_Gate
  nand nand_1 (nand_1_out, a, c);
  xor xor_1 (xor_1_out, ~b, ~c);  // XOR_Gate
  or or_1 (y, and_1_out, nand_1_out, xor_1_out);
endmodule

module zad3 (
  input  a,
  input  b,
  input  c,
  output out_4
);

  wire and_1_out, or_1_out, xor_1_out;

  and and_1 (and_1_out, a, ~b, c);  // AND_Gate
  xor xor_1 (xor_1_out, a, b);
  or or_1 (or_1_out, xor_1_out, c);
  or or_2 (out_4, and_1_out, or_1_out);
endmodule

module moduly (
  input  a,
  input  b,
  input  c,
  output out_4
);

  wire nand_1_out, nand_2_out, nand_3_out, nand_4_out, nand_5_out, xor_1_out;

  nand nand_1 (nand_1_out, a, ~b);  // NAND_Gate
  xor xor_1 (xor_1_out, a, b);
  not nand_2 (nand_2_out, nand_1_out);  // NAND_Gate
  nand nand_3 (nand_3_out, nand_2_out, c);
  nand nand_4 (nand_4_out, ~c, ~xor_1_out);  // NAND_Gate
  not nand_5 (nand_5_out, nand_3_out);  // NAND_Gate
  nand nand_6 (out_4, ~nand_5_out, ~nand_4_out);  // NAND_Gate
endmodule

module zad1_23_11 (
  input  a,
  input  b,
  input  c,
  input  d,
  output y
);

  wire nand_1_out, nand_2_out, nand_3_out, nand_4_out, nand_5_out, nand_6_out, nand_7_out, nand_8_out;

  nand nand_1 (nand_1_out, 1'b1, a);
  nand nand_2 (nand_2_out, 1'b1, b);
  nand nand_3 (nand_3_out, 1'b1, c);
  nand nand_4 (nand_4_out, 1'b1, d);
  nand nand_5 (nand_5_out, nand_1_out, nand_2_out, c, d);
  nand nand_6 (nand_6_out, a, nand_2_out, nand_3_out, nand_4_out);
  nand nand_7 (nand_7_out, a, b, nand_3_out, nand_4_out);
  nand nand_8 (nand_8_out, a, b, c, nand_4_out);
  nand nand_9 (y, nand_5_out, nand_6_out, nand_7_out, nand_8_out);
endmodule

module zad2_23_11 (
  input  a,
  input  b,
  input  c,
  output lewe,
  output prawe
);

  wire nor_1_out, nor_2_out, nor_3_out, nor_4_out, nor_5_out;

  not nor_1 (nor_1_out, ~a);  // NOR_Gate NOR_Gate
  not nor_2 (nor_2_out, c);  // NOR_Gate
  nor nor_3 (nor_3_out, ~b, ~c);  // NOR_Gate
  nor nor_4 (nor_4_out, nor_1_out, nor_2_out);
  nor nor_5 (nor_5_out, ~b, nor_4_out);  // NOR_Gate
  nor nor_6 (lewe, nor_3_out, nor_3_out);
  nor nor_7 (prawe, nor_5_out, nor_5_out);
endmodule

module zad2_30_11 (
  input  a,
  input  b,
  input  c,
  input  d,
  output y
);

  wire not_1_out;

  not not_1 (not_1_out, a);
  Multiplexer #(.select(3)) multiplexer_1 (
    .in0(not_1_out), .in1(1'b0), .in2(1'b0), .in3(1'b1), .in4(1'b0), .in5(1'b0), .in6(a), .in7(not_1_out),
    .out(y), .sel({b, c, d}));
endmodule

module zad1_30_11 (
  input  a,
  input  b,
  input  c,
  input  d,
  output y
);

  Multiplexer #(.select(4)) multiplexer_1 (
    .in0(1'b1), .in1(1'b0), .in2(1'b0), .in3(1'b1), .in4(1'b0), .in5(1'b0), .in6(1'b0), .in7(1'b1),
    .in8(1'b0), .in9(1'b0), .in10(1'b0), .in11(1'b1), .in12(1'b0), .in13(1'b0), .in14(1'b1), .in15(1'b0),
    .out(y), .sel({d, c, b, a}));
endmodule

module zad3_30_11 (
  input  [3:0] a,
  input  [3:0] b,
  output out_3
);

  wire adder_1_cout, adder_2_cout;

  Adder #(.width(3)) adder_1 (.a(a[3:1]), .b(b[3:1]), .cout(adder_1_cout));  // open: out, cin
  Adder #(.width(1)) adder_2 (.a(a[0]), .b(b[0]), .cin(adder_1_cout), .cout(adder_2_cout));  // open: out
  xor xor_1 (out_3, adder_1_cout, adder_2_cout);
endmodule

module zad4_30_11 (
  input  [3:0] a,
  input  [3:0] b,
  input  [1:0] operacja,
  output c,
  output z,
  output [3:0] out_6
);

  wire adder_1_cout, adder_2_cout;
  wire [0:0] adder_2_out;
  wire [2:0] adder_1_out;
  wire [3:0] and_1_out, negator_1_out, xor_1_out;

  assign xor_1_out = a ^ b;  // XOR_Gate xor_1, 4 bits wide
  assign and_1_out = a & b;  // AND_Gate and_1, 4 bits wide
  Adder #(.width(3)) adder_1 (.a(a[3:1]), .b(b[3:1]), .out(adder_1_out), .cout(adder_1_cout));  // open: cin
  Adder #(.width(1)) adder_2 (.a(a[0]), .b(b[0]), .out(adder_2_out[0]), .cin(adder_1_cout), .cout(adder_2_cout));
  xor xor_2 (c, adder_1_cout, adder_2_cout);
  Negator #(.width(4)) negator_1 (.in({adder_1_out, adder_2_out[0]}), .out(negator_1_out));
  Multiplexer #(.select(2), .width(4)) multiplexer_1 (
    .in0({adder_1_out, adder_2_out[0]}), .in1(negator_1_out), .in2(xor_1_out), .in3(and_1_out), .out(out_6),
    .sel(operacja));
  nor nor_1 (z, out_6[0], out_6[1], out_6[2], out_6[3]);
endmodule

module zad1_07_12 (
  input  in_1,
  input  in_2,
  input  in_3,
  output out_4
);

  wire d_ff_1_q, d_ff_2_q, d_ff_3_q;

  D_Flip_Flop d_ff_1 (.D(in_1), .clk(in_2), .Q(d_ff_1_q), .reset(in_3));  // open: Qn, preset
  D_Flip_Flop d_ff_2 (.D(d_ff_1_q), .clk(in_2), .Q(d_ff_2_q), .reset(in_3));  // open: Qn, preset
  D_Flip_Flop d_ff_3 (.D(d_ff_2_q), .clk(in_2), .Q(d_ff_3_q), .reset(in_3));  // open: Qn, preset
  D_Flip_Flop d_ff_4 (.D(d_ff_3_q), .clk(in_2), .Q(out_4), .reset(in_3));  // open: Qn, preset
endmodule

module zad2_07_12 (
  input  in_1,
  output out_2,
  output out_3,
  output out_4,
  output out_5
);

  wire clock_1_out;

  Clock clock_1 (.out(clock_1_out));
  D_Flip_Flop d_ff_1 (.D(out_5), .clk(clock_1_out), .Q(out_2), .preset(in_1));  // open: Qn, reset
  D_Flip_Flop d_ff_2 (.D(out_2), .clk(clock_1_out), .Q(out_3), .reset(in_1));  // open: Qn, preset
  D_Flip_Flop d_ff_3 (.D(out_3), .clk(clock_1_out), .Q(out_4), .reset(in_1));  // open: Qn, preset
  D_Flip_Flop d_ff_4 (.D(out_4), .clk(clock_1_out), .Q(out_5), .reset(in_1));  // open: Qn, preset
endmodule

module zad3_07_12 (
  output out_1,
  output out_2,
  output out_3,
  output out_4
);

  wire clock_1_out, d_ff_4_qn;

  Clock clock_1 (.out(clock_1_out));
  D_Flip_Flop d_ff_1 (.D(d_ff_4_qn), .clk(clock_1_out), .Q(out_1));  // open: Qn, preset, reset
  D_Flip_Flop d_ff_2 (.D(out_1), .clk(clock_1_out), .Q(out_2));  // open: Qn, preset, reset
  D_Flip_Flop d_ff_3 (.D(out_2), .clk(clock_1_out), .Q(out_3));  // open: Qn, preset, reset
  D_Flip_Flop d_ff_4 (.D(out_3), .clk(clock_1_out), .Q(out_4), .Qn(d_ff_4_qn));  // open: preset, reset
endmodule

module zad4_07_12 (
  input  in_1,
  output out_2,
  output out_3,
  output out_4,
  output out_5
);

  wire and_1_out, d_ff_1_qn, d_ff_2_qn, d_ff_3_qn, d_ff_4_qn;

  D_Flip_Flop d_ff_1 (.D(d_ff_1_qn), .clk(in_1), .Q(out_2), .Qn(d_ff_1_qn), .reset(and_1_out));  // open: preset
  D_Flip_Flop d_ff_2 (.D(d_ff_2_qn), .clk(d_ff_1_qn), .Q(out_3), .Qn(d_ff_2_qn), .reset(and_1_out));  // open: preset
  D_Flip_Flop d_ff_3 (.D(d_ff_3_qn), .clk(d_ff_2_qn), .Q(out_4), .Qn(d_ff_3_qn), .reset(and_1_out));  // open: preset
  D_Flip_Flop d_ff_4 (.D(d_ff_4_qn), .clk(d_ff_3_qn), .Q(out_5), .Qn(d_ff_4_qn), .reset(and_1_out));  // open: preset
  and and_1 (and_1_out, out_2, out_5);
endmodule

module zad5_07_12 (
  input  in_1,
  output out_2,
  output out_3,
  output out_4,
  output out_5
);

  wire and_1_out, d_ff_1_qn, d_ff_2_qn, d_ff_3_qn, d_ff_4_qn;

  D_Flip_Flop d_ff_1 (.D(d_ff_1_qn), .clk(in_1), .Q(out_2), .Qn(d_ff_1_qn), .preset(and_1_out));  // open: reset
  D_Flip_Flop d_ff_2 (.D(d_ff_2_qn), .clk(d_ff_1_qn), .Q(out_3), .Qn(d_ff_2_qn), .preset(and_1_out));  // open: reset
  D_Flip_Flop d_ff_3 (.D(d_ff_3_qn), .clk(d_ff_2_qn), .Q(out_4), .Qn(d_ff_3_qn), .reset(and_1_out));  // open: preset
  D_Flip_Flop d_ff_4 (.D(d_ff_4_qn), .clk(d_ff_3_qn), .Q(out_5), .Qn(d_ff_4_qn), .reset(and_1_out));  // open: preset
  and and_1 (and_1_out, out_3, out_5);
endmodule

module zad6_07_12 (
  output out_1,
  output out_2,
  output out_3,
  output out_4
);

  wire clock_1_out, xor_1_out;

  Clock clock_1 (.out(clock_1_out));
  D_Flip_Flop d_ff_1 (.D(xor_1_out), .clk(clock_1_out), .Q(out_1));  // open: Qn, preset, reset
  D_Flip_Flop d_ff_2 (.D(out_1), .clk(clock_1_out), .Q(out_2));  // open: Qn, preset, reset
  xor xor_1 (xor_1_out, out_4, out_3);
  D_Flip_Flop d_ff_3 (.D(out_2), .clk(clock_1_out), .Q(out_3));  // open: Qn, preset, reset
  D_Flip_Flop d_ff_4 (.D(out_3), .clk(clock_1_out), .Q(out_4));  // open: Qn, preset, reset
endmodule

module zad7_07_12 (
  input  in_1,
  input  in_2,
  input  in_3,
  output out_4,
  output out_5
);

  wire nand_1_out, nand_2_out;

  nand nand_1 (nand_1_out, in_1, in_2);
  nand nand_2 (nand_2_out, in_2, in_3);
  nand nand_3 (out_4, nand_1_out, out_5);
  nand nand_4 (out_5, out_4, nand_2_out);
endmodule

module zad8_07_12 (
  input  Onnn,
  input  Reset,
  input  Snap,
  output [3:0] out_4,
  output out_5,
  output [3:0] out_6
);

  wire clock_1_out;

  Clock clock_1 (.out(clock_1_out));
  D_Flip_Flop d_ff_1 (.D(Onnn), .clk(clock_1_out), .Q(out_4[0]), .reset(Reset));  // open: Qn, preset
  D_Flip_Flop d_ff_2 (.D(out_4[0]), .clk(Snap), .Q(out_6[0]));  // open: Qn, preset, reset
  D_Flip_Flop d_ff_3 (.D(out_4[0]), .clk(clock_1_out), .Q(out_4[1]), .reset(Reset));  // open: Qn, preset
  D_Flip_Flop d_ff_4 (.D(out_4[1]), .clk(Snap), .Q(out_6[1]));  // open: Qn, preset, reset
  D_Flip_Flop d_ff_5 (.D(out_4[1]), .clk(clock_1_out), .Q(out_4[2]), .reset(Reset));  // open: Qn, preset
  D_Flip_Flop d_ff_6 (.D(out_4[2]), .clk(Snap), .Q(out_6[2]));  // open: Qn, preset, reset
  D_Flip_Flop d_ff_7 (.D(out_4[2]), .clk(clock_1_out), .Q(out_4[3]), .reset(Reset));  // open: Qn, preset
  D_Flip_Flop d_ff_8 (.D(out_4[3]), .clk(Snap), .Q(out_6[3]));  // open: Qn, preset, reset

  assign out_5 = out_4[3];
endmodule

module zad1_14_12 (
  input  in_1
);

  wire clock_1_out, d_ff_1_qn, d_ff_2_qn, multiplexer_1_out, multiplexer_2_out, multiplexer_3_out;
  wire [1:0] d_ff_1_q;

  Clock clock_1 (.out(clock_1_out));
  D_Flip_Flop d_ff_1 (.D(d_ff_1_qn), .clk(clock_1_out), .Q(d_ff_1_q[0]), .Qn(d_ff_1_qn), .preset(in_1));  // open: reset
  Multiplexer #(.select(2)) multiplexer_1 (
    .in0(1'b1), .in1(1'b1), .in2(1'b0), .in3(1'b0), .out(multiplexer_1_out), .sel(d_ff_1_q));
  Multiplexer #(.select(2)) multiplexer_2 (
    .in0(1'b0), .in1(1'b1), .in2(1'b0), .in3(1'b1), .out(multiplexer_2_out), .sel(d_ff_1_q));
  Multiplexer #(.select(2)) multiplexer_3 (
    .in0(1'b0), .in1(1'b0), .in2(1'b1), .in3(1'b0), .out(multiplexer_3_out), .sel(d_ff_1_q));
  D_Flip_Flop d_ff_2 (.D(d_ff_2_qn), .clk(d_ff_1_qn), .Q(d_ff_1_q[1]), .Qn(d_ff_2_qn), .preset(in_1));  // open: reset
  LED led_1 (.in(multiplexer_1_out));
  LED led_2 (.in(multiplexer_2_out));
  LED led_3 (.in(multiplexer_3_out));
endmodule
